# Fritzing sketch schéma montage EXP (saved by Fritzing 0.9.3b)
breadboards: 1

parts:
  Composant1 = Arduino Uno (Rev3) - ICSP
  C1 = Ceramic Capacitor [capacitance=100nF package="100 mil [THT, multilayer]"]
  L1 = Inductor [package="400 mil [THT]"]
  R2 = Resistor [tolerance=±5% resistance=220 package=THT]
  LED1 = LED - 5mm [color="Red (633nm)" package="5 mm [THT]"]
  R3 = Resistor [tolerance=±5% resistance=220 package=THT]
  C2 = Ceramic Capacitor [capacitance=100nF package="100 mil [THT, multilayer]"]
  R4 = Resistor [tolerance=±5% resistance=220 package=THT]

nets:
  N1: Composant1.A0, LED1.cathode, R3.Pin_0, C2.0
  N2: Composant1.D9_PWM, R4.Pin_0
  N3: Composant1.GND, R3.Pin_1, C2.1
  N4: C1.1, L1.pin_0, LED1.anode
  N5: L1.pin_1, R2.Pin_0, R4.Pin_1
