# Fritzing sketch schéma montage VO (saved by Fritzing 0.9.3b)
breadboards: 2

parts:
  Composant1 = Arduino Uno (Rev3) - ICSP
  C1 = Ceramic Capacitor [capacitance=100nF package="100 mil [THT, multilayer]"]
  L1 = Inductor [package="400 mil [THT]"]
  R2 = Resistor [tolerance=±5% resistance=220 package=THT]
  R3 = Resistor [tolerance=±5% resistance=220 package=THT]
  C2 = Ceramic Capacitor [capacitance=100nF package="100 mil [THT, multilayer]"]
  D1 = Rectifier Diode [part_number=1N4001 package="300 mil [THT]"]
  R4 = Resistor [tolerance=±5% resistance=220 package=THT]
  R5 = Resistor [tolerance=±5% resistance=220 package=THT]
  LED1 = LED - 5mm [color="Red (633nm)" package="5 mm [THT]"]
  LED2 = LED - 5mm [color="Red (633nm)" package="5 mm [THT]"]
  LED3 = LED - 5mm [color="Red (633nm)" package="5 mm [THT]"]
  R6 = Resistor [tolerance=±5% resistance=220 package=THT]
  R7 = Resistor [tolerance=±5% resistance=220 package=THT]

nets:
  N1: Composant1.A0, D1.cathode
  N2: Composant1.D2, R5.Pin_0
  N3: Composant1.D3_PWM, R7.Pin_0
  N4: Composant1.D4, R6.Pin_0
  N5: Composant1.GND, R3.Pin_1, C2.1, LED1.cathode, LED2.cathode, LED3.cathode
  N6: C1.1, L1.pin_0, D1.anode
  N7: L1.pin_1, R2.Pin_0, R4.Pin_1
  N8: R3.Pin_0, C2.0
  N9: R5.Pin_1, LED1.anode
  N10: LED2.anode, R7.Pin_1
  N11: LED3.anode, R6.Pin_1
